// Logisim project FMS.circ as structural Verilog: 2 circuits, main circuit circuito_ttl
module main (
  input  S,
  input  V
);

  wire and_1_out, and_2_out, and_3_out, and_4_out, and_5_out, and_6_out, and_7_out, and_8_out, button_1_out,
       clock_1_out, d_ff_1_q, d_ff_1_qn, d_ff_2_q, d_ff_2_qn, not_1_out, or_1_out;

  not not_1 (not_1_out, V);
  and and_1 (and_1_out, S, d_ff_1_qn);
  and and_2 (and_2_out, d_ff_1_q, not_1_out);
  and and_3 (and_3_out, d_ff_1_q, d_ff_2_qn);
  Clock clock_1 (.out(clock_1_out));
  or or_1 (or_1_out, and_1_out, and_2_out);
  Button button_1 (.out(button_1_out));
  D_Flip_Flop d_ff_1 (
    .D(and_4_out), .clk(clock_1_out), .Q(d_ff_1_q), .Qn(d_ff_1_qn), .reset(button_1_out));  // open: preset
  D_Flip_Flop d_ff_2 (
    .D(and_3_out), .clk(clock_1_out), .Q(d_ff_2_q), .Qn(d_ff_2_qn), .reset(button_1_out));  // open: preset
  // Probe on d_ff_1_q
  // Probe on d_ff_2_q
  and and_4 (and_4_out, d_ff_2_qn, or_1_out);
  // Probe on and_4_out
  and and_5 (and_5_out, d_ff_1_qn, d_ff_2_qn);
  and and_6 (and_6_out, d_ff_1_q, d_ff_2_qn);
  and and_7 (and_7_out, d_ff_2_q, d_ff_1_qn);
  and and_8 (and_8_out, d_ff_1_q, d_ff_2_q);
  LED Aguardando (.in(and_5_out));
  LED Validando (.in(and_6_out));
  LED Aceito (.in(and_7_out));
  LED Negado (.in(and_8_out));

  // Notes on the sheet:
  //   d1
  //   d0
  //   Q0
  //   Q1
endmodule

module circuito_ttl (
  input  V,
  input  S
);

  wire clock_1_out, n7408_1_pin1, n7408_1_pin2, n7408_1_pin3, n7408_1_pin4, n7408_1_pin5, n7408_1_pin6,
       n7408_1_pin7, n7408_1_pin8, n7408_1_pin10, n7408_1_pin11, n7408_1_pin14, n7408_2_pin3, n7408_2_pin6,
       n7408_2_pin8, n7408_2_pin11, n7474_1_pin5;

  Clock clock_1 (.out(clock_1_out));
  _7408 #(.VccGndPorts("true")) u_7408_1 (
    .pin1(n7408_1_pin1), .pin2(n7408_1_pin2), .pin3(n7408_1_pin3), .pin4(n7408_1_pin4), .pin5(n7408_1_pin5),
    .pin6(n7408_1_pin6), .pin7(n7408_1_pin7), .pin14(n7408_1_pin14), .pin13(n7408_1_pin5),
    .pin12(n7408_1_pin1), .pin11(n7408_1_pin11), .pin10(n7408_1_pin10), .pin9(S), .pin8(n7408_1_pin8));
  _7474 #(.VccGndPorts("true")) u_7474_1 (
    .pin1(n7408_1_pin14), .pin2(n7408_1_pin11), .pin3(clock_1_out), .pin4(n7408_1_pin14),
    .pin5(n7474_1_pin5), .pin6(n7408_1_pin5), .pin7(n7408_1_pin7), .pin14(n7408_1_pin14),
    .pin13(n7408_1_pin14), .pin12(n7408_1_pin6), .pin11(clock_1_out), .pin10(n7408_1_pin14),
    .pin9(n7408_1_pin1), .pin8(n7408_1_pin10));
  _7404 #(.VccGndPorts("true")) u_7404_1 (
    .pin7(n7408_1_pin7), .pin14(n7408_1_pin14), .pin13(V), .pin12(n7408_1_pin2));  // open: pin1, pin2, pin3, pin4, pin5, pin6, pin11, pin10, pin9, pin8
  _7432 #(.VccGndPorts("true")) u_7432_1 (
    .pin7(n7408_1_pin7), .pin14(n7408_1_pin14), .pin13(n7408_1_pin3), .pin12(n7408_1_pin8),
    .pin11(n7408_1_pin4));  // open: pin1, pin2, pin3, pin4, pin5, pin6, pin10, pin9, pin8
  _7408 #(.VccGndPorts("true")) u_7408_2 (
    .pin1(n7474_1_pin5), .pin2(n7408_1_pin10), .pin3(n7408_2_pin3), .pin4(n7474_1_pin5), .pin5(n7408_1_pin1),
    .pin6(n7408_2_pin6), .pin7(n7408_1_pin7), .pin14(n7408_1_pin14), .pin13(n7408_1_pin10),
    .pin12(n7408_1_pin5), .pin11(n7408_2_pin11), .pin10(n7408_1_pin5), .pin9(n7408_1_pin1),
    .pin8(n7408_2_pin8));
  LED Aguardando (.in(n7408_2_pin11));
  LED Validando (.in(n7408_2_pin8));
  LED Aceito (.in(n7408_2_pin3));
  LED Negado (.in(n7408_2_pin6));
  // Buzzer #(.vol_width(8)) buzzer_1: pin names not known; wires that end beside it: n7408_2_pin6, n7408_2_pin6
  // also tied to GND on the sheet: n7408_1_pin7
  // also tied to VCC on the sheet: n7408_1_pin14

  // Notes on the sheet:
  //   D0
  //   D1
  //   D1
  //   ~Q0
  //   Q1
  //   Q0
  //   ~Q0
  //   D0
endmodule
